# Fritzing sketch DeathWatch (saved by Fritzing 0.9.3b)
breadboards: 1

parts:
  R1_Pull-Up = Resistor [tolerance=±5% resistance=3.3k package=THT]
  5V_from_ESP32 = DC Power [voltage=5]
  DS2 = DS18B20 1-Wire Temperature Sensor [part_number=DS18B20]
  Motion = PIR sensor
  Ultrasonic = SRF05 Ultrasonic Rangefinder [part_number=HC-SR04-P]
  ESP32 = ESP32 Module Testbed

nets:
  N1: R1_Pull-Up.Pin_0, DS2.DQ
  VDD: R1_Pull-Up.Pin_1, DS2.VDD, Ultrasonic.VCC, ESP32.3V3
  N2: 5V_from_ESP32.V+, Motion.VDD
  N3: DS2.GND, ESP32.GND#51
  N4: Motion.SIG, ESP32.IO34, ESP32.IO17
  N5: Motion.GND, ESP32.GND#0
  N6: Ultrasonic.Trig, ESP32.IO15
  N7: Ultrasonic.Echo, ESP32.IO4
  N8: Ultrasonic.GND, ESP32.GND#85

custom parts:
  ESP32 Module Testbed: The ESP32 Module Testbed is a breadboard compatible breakout board for the ESP-WROOM-03 ESP32 module. The ESP32 is a WiFi and Bluetooth-enabled 32-bit, dual-core microcontroller.
